# Fritzing sketch Schematicfzz (saved by Fritzing 0.8.7b)
breadboards: 1

parts:
  Arduino_Uno = Arduino Uno (Rev3)
  U1 = L298 [package=multiwatt15_6400bgheatsink]
  U2 = 74HC595 [package="DIP16 [THT]"]
  U3 = 74HC595 [package="DIP16 [THT]"]
  Verb_Status_(Gelb) = LED - 5mm [color="Yellow (574nm)" package="5 mm [THT]"]
  R1 = Resistor [tolerance=±5% resistance=1k package=THT]
  Fehlerstatus_(Rot) = LED - 5mm [color="Yellow (574nm)" package="5 mm [THT]"]
  R2 = Resistor [tolerance=±5% resistance=1k package=THT]
  X1 = DB25 [package=db25]
  X2 = DB25 [package=db25]
  J1 = Screw terminal - 2 pins [package=THT]
  J2 = Screw terminal - 2 pins [package=THT]
  D1 = Rectifier Diode [part_number=1N4001 package="300 mil [THT]"]
  D2 = Rectifier Diode [part_number=1N4001 package="300 mil [THT]"]
  D3 = Rectifier Diode [part_number=1N4001 package="300 mil [THT]"]
  D4 = Rectifier Diode [part_number=1N4001 package="300 mil [THT]"]
  D5 = Rectifier Diode [part_number=1N4001 package="300 mil [THT]"]
  D6 = Rectifier Diode [part_number=1N4001 package="300 mil [THT]"]
  D7 = Rectifier Diode [part_number=1N4001 package="300 mil [THT]"]
  D8 = Rectifier Diode [part_number=1N4001 package="300 mil [THT]"]

nets:
  N1: Arduino_Uno.A0, Verb_Status_(Gelb).anode
  N2: Arduino_Uno.A1, Fehlerstatus_(Rot).anode
  GND: Arduino_Uno.GND, U1.CSA, U1.GND, U1.CSB, U2.GND, U2.OE, U3.GND, U3.OE, R1.Pin_1, R2.Pin_1, X1.25, D1.anode, D2.anode, D3.anode, D4.anode
  N3: Arduino_Uno.D2, U2.MR, U3.MR
  N4: Arduino_Uno.D3_PWM, U2.SH_CP, U3.SH_CP
  N5: Arduino_Uno.D4, U2.ST_CP, U3.ST_CP
  N6: Arduino_Uno.D5_PWM, U3.DS
  N7: U1.OUT1, J1.pin1, D1.cathode, D8.anode
  N8: U1.OUT2, J1.pin2, D2.cathode, D7.anode
  12V: U1.VS, D5.cathode, D6.cathode, D7.cathode, D8.cathode
  N9: U1.IN1, X2.1
  N10: U1.ENA, U1.ENB
  N11: U1.IN2, X2.2
  5V: U1.VLS, U2.VCC, U3.VCC, X1.24
  N12: U1.IN3, X2.3
  N13: U1.IN4, X2.4
  N14: U1.OUT3, J2.pin1, D3.cathode, D6.anode
  N15: U1.OUT4, J2.pin2, D4.cathode, D5.anode
  N16: U2.Q1, X1.10
  N17: U2.Q2, X1.11
  N18: U2.Q3, X1.12
  N19: U2.Q4, X1.13
  Naechstes Schieberegister (DS): U2.Q7'
  N20: U2.DS, U3.Q7'
  N21: U2.Q0, X1.9
  N22: U3.Q1, X1.2
  N23: U3.Q2, X1.3
  N24: U3.Q3, X1.4
  N25: U3.Q4, X1.5
  N26: U3.Q5, X1.6
  N27: U3.Q6, X1.7
  N28: U3.Q7, X1.8
  N29: U3.Q0, X1.1
  N30: Verb_Status_(Gelb).cathode, R1.Pin_0
  N31: Fehlerstatus_(Rot).cathode, R2.Pin_0

notes:
  Weichensteuerung Bahnhof, Treiberplatine, unter Modulen, direkt mit Weichen verbunden, 1.1
  Weichensteuerung Bahnhof, Steuerungsplatine, direkte Verbindung zum PC, 1.1
  ...
  5x pro Platine
